// Logisim project LogismInterruptAndPolling.circ as structural Verilog: 27 circuits, main circuit cpu
module cpu (
  input  [15:0] datOut,
  input  clock,
  input  \int ,
  output [11:0] addr,
  output [15:0] DataIn,
  output memWrt,
  output intack
);

  wire alu_1_zero_flag, control_unit_1_cli, control_unit_1_flagld, control_unit_1_intld, control_unit_1_irld,
       control_unit_1_pc_minus_minus, control_unit_1_pc_plus_plus, control_unit_1_pcld, control_unit_1_regld,
       control_unit_1_ret, control_unit_1_sp_minus_minus, control_unit_1_sp_plus_plus, control_unit_1_sti,
       control_unit_1_zf_ld;
  wire [1:0] control_unit_1_armux0;
  wire [2:0] control_unit_1_mux0;
  wire [3:0] myregister_1_output_2;
  wire [11:0] adder_1_out, adder_3_out, multiplexer_1_out, multiplexer_5_out, myregister_1_output,
       n12bitreg_1_output, regi_ster_bank_1_out_19, register7_1_output_2;
  wire [15:0] adder_2_out, alu_1_aluoutput, multiplexer_4_out, regi_ster_bank_1_out_12,
       regi_ster_bank_1_out_13, regi_ster_bank_1_out_14, regi_ster_bank_1_out_15, regi_ster_bank_1_out_16,
       regi_ster_bank_1_out_17, regi_ster_bank_1_out_18, undriven;
  wire [15:12] multiplexer_5_out_2, regi_ster_bank_1_out_19_2, register7_1_output;

  Adder_part #(.width(12)) adder_1 (
    .a(myregister_1_output), .b(register7_1_output_2), .out(adder_1_out));  // open: cin, cout
  Control_Unit control_unit_1 (
    .MemLd(memWrt), .ZfFlag_regbank(regi_ster_bank_1_out_18[0]),
    .int_flag_regBank(regi_ster_bank_1_out_18[1]), .\int (\int ), .Opcode(datOut[15:12]),
    .PC_minus_minus(control_unit_1_pc_minus_minus), .SP_minus_minus(control_unit_1_sp_minus_minus),
    .SP_plus_plus(control_unit_1_sp_plus_plus), .irLd(control_unit_1_irld), .mux0(control_unit_1_mux0[0]),
    .mux1(control_unit_1_mux0[1]), .next(control_unit_1_mux0[2]), .zf_ld(control_unit_1_zf_ld),
    .regLd(control_unit_1_regld), .ArMux0(control_unit_1_armux0[0]), .ArMux1(control_unit_1_armux0[1]),
    .PC_plus_plus(control_unit_1_pc_plus_plus), .PcLd(control_unit_1_pcld), .ret(control_unit_1_ret),
    .Cli(control_unit_1_cli), .Sti(control_unit_1_sti), .flagld(control_unit_1_flagld),
    .intld(control_unit_1_intld), .intach(intack), .clk(clock));
  Multiplexer #(.width(12)) multiplexer_1 (
    .in0(adder_1_out), .in1(DataIn[11:0]), .out(multiplexer_1_out), .sel(control_unit_1_ret));  // open: en
  Multiplexer #(.select(2), .width(12)) multiplexer_2 (
    .in0(register7_1_output_2), .in1(multiplexer_5_out), .in2(regi_ster_bank_1_out_19),
    .in3(n12bitreg_1_output), .out(addr), .sel(control_unit_1_armux0));  // open: en
  register7 register7_1 (
    .\input ({4'b0000, multiplexer_1_out}), .SP_plus_plus(control_unit_1_pc_plus_plus),
    .SP_minus_minus(control_unit_1_pc_minus_minus), .ld(control_unit_1_pcld), .clock(clock),
    .\output ({register7_1_output, register7_1_output_2}));
  \REGİSTER__BANK  \regi̇ster_bank_1  (
    .CLI(control_unit_1_cli), .STI(control_unit_1_sti), .ZfLoad_Ctrl(control_unit_1_zf_ld),
    .Zf_ALU(alu_1_zero_flag), .flagld(control_unit_1_flagld), .SP_plus_plus(control_unit_1_sp_plus_plus),
    .SP_minus_minus(control_unit_1_sp_minus_minus), .RegBankInp(DataIn), .RegBankLd(control_unit_1_regld),
    .RegSelect(myregister_1_output[2:0]), .clock(clock), .out_12(regi_ster_bank_1_out_12),
    .out_13(regi_ster_bank_1_out_13), .out_14(regi_ster_bank_1_out_14), .out_15(regi_ster_bank_1_out_15),
    .out_16(regi_ster_bank_1_out_16), .out_17(regi_ster_bank_1_out_17), .out_18(regi_ster_bank_1_out_18),
    .out_19({regi_ster_bank_1_out_19_2, regi_ster_bank_1_out_19}));
  Multiplexer #(.select(3), .width(16)) multiplexer_3 (
    .in0(datOut), .in1(multiplexer_4_out), .in2({multiplexer_5_out_2, multiplexer_5_out}),
    .in3(alu_1_aluoutput), .in4({4'b0000, register7_1_output_2}), .in5(regi_ster_bank_1_out_18),
    .out(DataIn), .sel(control_unit_1_mux0));  // open: in6, in7, en
  Multiplexer #(.select(3), .width(16)) multiplexer_4 (
    .in0(regi_ster_bank_1_out_12), .in1(regi_ster_bank_1_out_13), .in2(regi_ster_bank_1_out_14),
    .in3(regi_ster_bank_1_out_15), .in4(regi_ster_bank_1_out_16), .in5(regi_ster_bank_1_out_17),
    .in6(regi_ster_bank_1_out_18), .in7({regi_ster_bank_1_out_19_2, regi_ster_bank_1_out_19}),
    .out(multiplexer_4_out), .sel(myregister_1_output[8:6]));  // open: en
  ALU alu_1 (
    .control_inp_2(myregister_1_output[8:6]), .Control_inpt(myregister_1_output[11:9]),
    .input2(multiplexer_4_out), .input1({multiplexer_5_out_2, multiplexer_5_out}),
    .aluoutput(alu_1_aluoutput), .zero_flag(alu_1_zero_flag));
  Multiplexer #(.select(3), .width(16)) multiplexer_5 (
    .in0(regi_ster_bank_1_out_12), .in1(regi_ster_bank_1_out_13), .in2(regi_ster_bank_1_out_14),
    .in3(regi_ster_bank_1_out_15), .in4(regi_ster_bank_1_out_16), .in5(regi_ster_bank_1_out_17),
    .in6(regi_ster_bank_1_out_18), .in7({regi_ster_bank_1_out_19_2, regi_ster_bank_1_out_19}),
    .out({multiplexer_5_out_2, multiplexer_5_out}), .sel(myregister_1_output[5:3]));  // open: en
  Adder_part #(.width(16)) adder_2 (.a(16'h1), .b(undriven), .out(adder_2_out));  // open: cin, cout
  myRegister myregister_1 (
    .\input (datOut), .ld(control_unit_1_irld), .clock(clock),
    .\output ({myregister_1_output_2, myregister_1_output}));  // open: reset
  Adder_part #(.width(12)) adder_3 (.a(datOut[11:0]), .b(12'h7f0), .out(adder_3_out));  // open: cin, cout
  _12bitreg u_12bitreg_1 (
    .\input (adder_3_out), .load(control_unit_1_intld), .clock(clock), .\output (n12bitreg_1_output));  // open: reset
endmodule

module Adder (
  input  [15:0] bi,
  input  [15:0] di,
  output carry,
  output [15:0] result
);

  wire halfadder_1_ci_1, halfadder_3_ci_1, halfadder_4_ci_1, halfadder_5_ci_1, halfadder_6_ci_1,
       halfadder_7_ci_1, halfadder_8_ci_1, halfadder_9_ci_1, halfadder_10_ci_1, halfadder_11_ci_1,
       halfadder_12_ci_1, halfadder_13_ci_1, halfadder_14_ci_1, halfadder_15_ci_1, halfadder_16_ci_1;

  HalfAdder halfadder_1 (.d(di[14]), .b(bi[14]), .ci(halfadder_3_ci_1), .ci_1(halfadder_1_ci_1), .r(result[14]));
  HalfAdder halfadder_2 (.d(di[15]), .b(bi[15]), .ci(halfadder_1_ci_1), .ci_1(carry), .r(result[15]));
  HalfAdder halfadder_3 (.d(di[13]), .b(bi[13]), .ci(halfadder_4_ci_1), .ci_1(halfadder_3_ci_1), .r(result[13]));
  HalfAdder halfadder_4 (.d(di[12]), .b(bi[12]), .ci(halfadder_5_ci_1), .ci_1(halfadder_4_ci_1), .r(result[12]));
  HalfAdder halfadder_5 (.d(di[11]), .b(bi[11]), .ci(halfadder_7_ci_1), .ci_1(halfadder_5_ci_1), .r(result[11]));
  HalfAdder halfadder_6 (.d(di[9]), .b(bi[9]), .ci(halfadder_8_ci_1), .ci_1(halfadder_6_ci_1), .r(result[9]));
  HalfAdder halfadder_7 (.d(di[10]), .b(bi[10]), .ci(halfadder_6_ci_1), .ci_1(halfadder_7_ci_1), .r(result[10]));
  HalfAdder halfadder_8 (.d(di[8]), .b(bi[8]), .ci(halfadder_9_ci_1), .ci_1(halfadder_8_ci_1), .r(result[8]));
  HalfAdder halfadder_9 (.d(di[7]), .b(bi[7]), .ci(halfadder_10_ci_1), .ci_1(halfadder_9_ci_1), .r(result[7]));
  HalfAdder halfadder_10 (.d(di[6]), .b(bi[6]), .ci(halfadder_11_ci_1), .ci_1(halfadder_10_ci_1), .r(result[6]));
  HalfAdder halfadder_11 (.d(di[5]), .b(bi[5]), .ci(halfadder_12_ci_1), .ci_1(halfadder_11_ci_1), .r(result[5]));
  HalfAdder halfadder_12 (.d(di[4]), .b(bi[4]), .ci(halfadder_13_ci_1), .ci_1(halfadder_12_ci_1), .r(result[4]));
  HalfAdder halfadder_13 (.d(di[3]), .b(bi[3]), .ci(halfadder_15_ci_1), .ci_1(halfadder_13_ci_1), .r(result[3]));
  HalfAdder halfadder_14 (.d(di[1]), .b(bi[1]), .ci(halfadder_16_ci_1), .ci_1(halfadder_14_ci_1), .r(result[1]));
  HalfAdder halfadder_15 (.d(di[2]), .b(bi[2]), .ci(halfadder_14_ci_1), .ci_1(halfadder_15_ci_1), .r(result[2]));
  HalfAdder halfadder_16 (.d(di[0]), .b(bi[0]), .ci(1'b0), .ci_1(halfadder_16_ci_1), .r(result[0]));
endmodule

module HalfAdder (
  input  d,
  input  b,
  input  ci,
  output ci_1,
  output r
);

  wire and_1_out, and_2_out, and_3_out, and_4_out, and_5_out, and_6_out, and_7_out, not_1_out, not_2_out,
       not_3_out;

  not not_1 (not_1_out, d);
  and and_1 (and_1_out, b, d);
  or or_1 (ci_1, and_4_out, and_1_out, and_7_out);
  and and_2 (and_2_out, d, b, ci);
  not not_2 (not_2_out, b);
  and and_3 (and_3_out, not_1_out, not_2_out, ci);
  and and_4 (and_4_out, d, ci);
  or or_2 (r, and_2_out, and_3_out, and_5_out, and_6_out);
  and and_5 (and_5_out, not_1_out, b, not_3_out);
  and and_6 (and_6_out, d, not_2_out, not_3_out);
  not not_3 (not_3_out, ci);
  and and_7 (and_7_out, b, ci);
endmodule

module HalfSubt (
  input  a,
  input  b,
  input  ci,
  output ci_1,
  output r
);

  wire and_1_out, and_2_out, and_3_out, and_4_out, and_5_out, and_6_out, and_7_out, not_1_out, not_2_out,
       not_3_out;

  not not_1 (not_1_out, a);
  and and_1 (and_1_out, b, ci);
  or or_1 (ci_1, and_4_out, and_1_out, and_7_out);
  and and_2 (and_2_out, a, not_2_out, not_3_out);
  not not_2 (not_2_out, b);
  and and_3 (and_3_out, a, b, ci);
  and and_4 (and_4_out, not_1_out, b);
  or or_2 (r, and_2_out, and_3_out, and_5_out, and_6_out);
  and and_5 (and_5_out, not_1_out, not_2_out, ci);
  and and_6 (and_6_out, not_1_out, b, not_3_out);
  not not_3 (not_3_out, ci);
  and and_7 (and_7_out, not_1_out, ci);
endmodule

module Subtractor (
  input  [15:0] ai,
  input  [15:0] bi,
  output carry,
  output [15:0] result
);

  wire halfsubt_1_ci_1, halfsubt_3_ci_1, halfsubt_4_ci_1, halfsubt_5_ci_1, halfsubt_6_ci_1, halfsubt_7_ci_1,
       halfsubt_8_ci_1, halfsubt_9_ci_1, halfsubt_10_ci_1, halfsubt_11_ci_1, halfsubt_12_ci_1,
       halfsubt_13_ci_1, halfsubt_14_ci_1, halfsubt_15_ci_1, halfsubt_16_ci_1;

  HalfSubt halfsubt_1 (.a(ai[14]), .b(bi[14]), .ci(halfsubt_3_ci_1), .ci_1(halfsubt_1_ci_1), .r(result[14]));
  HalfSubt halfsubt_2 (.a(ai[15]), .b(bi[15]), .ci(halfsubt_1_ci_1), .ci_1(carry), .r(result[15]));
  HalfSubt halfsubt_3 (.a(ai[13]), .b(bi[13]), .ci(halfsubt_5_ci_1), .ci_1(halfsubt_3_ci_1), .r(result[13]));
  HalfSubt halfsubt_4 (.a(ai[11]), .b(bi[11]), .ci(halfsubt_6_ci_1), .ci_1(halfsubt_4_ci_1), .r(result[11]));
  HalfSubt halfsubt_5 (.a(ai[12]), .b(bi[12]), .ci(halfsubt_4_ci_1), .ci_1(halfsubt_5_ci_1), .r(result[12]));
  HalfSubt halfsubt_6 (.a(ai[10]), .b(bi[10]), .ci(halfsubt_7_ci_1), .ci_1(halfsubt_6_ci_1), .r(result[10]));
  HalfSubt halfsubt_7 (.a(ai[9]), .b(bi[9]), .ci(halfsubt_8_ci_1), .ci_1(halfsubt_7_ci_1), .r(result[9]));
  HalfSubt halfsubt_8 (.a(ai[8]), .b(bi[8]), .ci(halfsubt_10_ci_1), .ci_1(halfsubt_8_ci_1), .r(result[8]));
  HalfSubt halfsubt_9 (.a(ai[6]), .b(bi[6]), .ci(halfsubt_11_ci_1), .ci_1(halfsubt_9_ci_1), .r(result[6]));
  HalfSubt halfsubt_10 (.a(ai[7]), .b(bi[7]), .ci(halfsubt_9_ci_1), .ci_1(halfsubt_10_ci_1), .r(result[7]));
  HalfSubt halfsubt_11 (.a(ai[5]), .b(bi[5]), .ci(halfsubt_12_ci_1), .ci_1(halfsubt_11_ci_1), .r(result[5]));
  HalfSubt halfsubt_12 (.a(ai[4]), .b(bi[4]), .ci(halfsubt_13_ci_1), .ci_1(halfsubt_12_ci_1), .r(result[4]));
  HalfSubt halfsubt_13 (.a(ai[3]), .b(bi[3]), .ci(halfsubt_14_ci_1), .ci_1(halfsubt_13_ci_1), .r(result[3]));
  HalfSubt halfsubt_14 (.a(ai[2]), .b(bi[2]), .ci(halfsubt_15_ci_1), .ci_1(halfsubt_14_ci_1), .r(result[2]));
  HalfSubt halfsubt_15 (.a(ai[1]), .b(bi[1]), .ci(halfsubt_16_ci_1), .ci_1(halfsubt_15_ci_1), .r(result[1]));
  HalfSubt halfsubt_16 (.a(ai[0]), .b(bi[0]), .ci(1'b0), .ci_1(halfsubt_16_ci_1), .r(result[0]));
endmodule

module And_16_bits (
  input  [15:0] a,
  input  [15:0] b,
  output [15:0] result
);

  and and_1 (result[14], a[14], b[14]);
  and and_2 (result[15], a[15], b[15]);
  and and_3 (result[13], a[13], b[13]);
  and and_4 (result[12], a[12], b[12]);
  and and_5 (result[11], a[11], b[11]);
  and and_6 (result[10], a[10], b[10]);
  and and_7 (result[8], a[8], b[8]);
  and and_8 (result[9], a[9], b[9]);
  and and_9 (result[7], a[7], b[7]);
  and and_10 (result[6], a[6], b[6]);
  and and_11 (result[5], a[5], b[5]);
  and and_12 (result[4], a[4], b[4]);
  and and_13 (result[2], a[2], b[2]);
  and and_14 (result[3], a[3], b[3]);
  and and_15 (result[0], a[0], b[0]);
  and and_16 (result[1], a[1], b[1]);
endmodule

module Or_16_bits (
  input  [15:0] a,
  input  [15:0] b,
  output [15:0] result
);

  or or_1 (result[15], a[15], b[15]);
  or or_2 (result[14], a[14], b[14]);
  or or_3 (result[13], a[13], b[13]);
  or or_4 (result[12], a[12], b[12]);
  or or_5 (result[10], a[10], b[10]);
  or or_6 (result[11], a[11], b[11]);
  or or_7 (result[8], a[8], b[8]);
  or or_8 (result[9], a[9], b[9]);
  or or_9 (result[7], a[7], b[7]);
  or or_10 (result[6], a[6], b[6]);
  or or_11 (result[4], a[4], b[4]);
  or or_12 (result[5], a[5], b[5]);
  or or_13 (result[3], a[3], b[3]);
  or or_14 (result[2], a[2], b[2]);
  or or_15 (result[0], a[0], b[0]);
  or or_16 (result[1], a[1], b[1]);
endmodule

module Xor_16_bits (
  input  [15:0] a,
  input  [15:0] b,
  output [15:0] result
);

  xor xor_1 (result[15], a[15], b[15]);
  xor xor_2 (result[14], a[14], b[14]);
  xor xor_3 (result[13], a[13], b[13]);
  xor xor_4 (result[11], a[11], b[11]);
  xor xor_5 (result[12], a[12], b[12]);
  xor xor_6 (result[9], a[9], b[9]);
  xor xor_7 (result[10], a[10], b[10]);
  xor xor_8 (result[7], a[7], b[7]);
  xor xor_9 (result[8], a[8], b[8]);
  xor xor_10 (result[6], a[6], b[6]);
  xor xor_11 (result[5], a[5], b[5]);
  xor xor_12 (result[3], a[3], b[3]);
  xor xor_13 (result[4], a[4], b[4]);
  xor xor_14 (result[2], a[2], b[2]);
  xor xor_15 (result[1], a[1], b[1]);
  xor xor_16 (result[0], a[0], b[0]);
endmodule

module Not_16_bits (
  input  [15:0] in_1,
  output [15:0] out_2
);

  not not_1 (out_2[15], in_1[15]);
  not not_2 (out_2[11], in_1[11]);
  not not_3 (out_2[14], in_1[14]);
  not not_4 (out_2[13], in_1[13]);
  not not_5 (out_2[12], in_1[12]);
  not not_6 (out_2[8], in_1[8]);
  not not_7 (out_2[9], in_1[9]);
  not not_8 (out_2[10], in_1[10]);
  not not_9 (out_2[7], in_1[7]);
  not not_10 (out_2[6], in_1[6]);
  not not_11 (out_2[5], in_1[5]);
  not not_12 (out_2[3], in_1[3]);
  not not_13 (out_2[4], in_1[4]);
  not not_14 (out_2[1], in_1[1]);
  not not_15 (out_2[2], in_1[2]);
  not not_16 (out_2[0], in_1[0]);
endmodule

module Inc_16_bits (
  input  [15:0] \input ,
  output carry,
  output [15:0] \output 
);

  wire and_2_out, and_3_out, and_4_out, and_5_out, and_6_out, and_7_out, and_8_out, and_9_out, and_10_out,
       and_11_out, and_12_out, and_13_out, and_14_out, and_15_out, and_16_out;

  and and_1 (carry, and_2_out, \input [15]);
  and and_2 (and_2_out, and_3_out, \input [14]);
  xor xor_1 (\output [15], and_2_out, \input [15]);
  and and_3 (and_3_out, and_4_out, \input [13]);
  xor xor_2 (\output [14], and_3_out, \input [14]);
  and and_4 (and_4_out, and_5_out, \input [12]);
  xor xor_3 (\output [13], and_4_out, \input [13]);
  and and_5 (and_5_out, and_6_out, \input [11]);
  xor xor_4 (\output [12], and_5_out, \input [12]);
  and and_6 (and_6_out, and_7_out, \input [10]);
  xor xor_5 (\output [11], and_6_out, \input [11]);
  and and_7 (and_7_out, and_8_out, \input [9]);
  xor xor_6 (\output [10], and_7_out, \input [10]);
  and and_8 (and_8_out, and_9_out, \input [8]);
  xor xor_7 (\output [9], and_8_out, \input [9]);
  and and_9 (and_9_out, and_10_out, \input [7]);
  xor xor_8 (\output [8], and_9_out, \input [8]);
  and and_10 (and_10_out, and_11_out, \input [6]);
  xor xor_9 (\output [7], and_10_out, \input [7]);
  and and_11 (and_11_out, and_12_out, \input [5]);
  xor xor_10 (\output [6], and_11_out, \input [6]);
  and and_12 (and_12_out, and_13_out, \input [4]);
  xor xor_11 (\output [5], and_12_out, \input [5]);
  and and_13 (and_13_out, and_14_out, \input [3]);
  xor xor_12 (\output [4], and_13_out, \input [4]);
  and and_14 (and_14_out, and_15_out, \input [2]);
  xor xor_13 (\output [3], and_14_out, \input [3]);
  and and_15 (and_15_out, and_16_out, \input [1]);
  xor xor_14 (\output [2], and_15_out, \input [2]);
  and and_16 (and_16_out, 1'b1, \input [0]);
  xor xor_15 (\output [1], and_16_out, \input [1]);
  xor xor_16 (\output [0], 1'b1, \input [0]);
endmodule

module Decrementer (
  input  [15:0] \input ,
  output carry_flag,
  output [15:0] \output 
);

  wire and_2_out, and_3_out, and_4_out, and_5_out, and_6_out, and_7_out, and_8_out, and_9_out, and_10_out,
       and_11_out, and_12_out, and_13_out, and_14_out, and_15_out, not_1_out, not_2_out, not_3_out,
       not_4_out, not_5_out, not_6_out, not_7_out, not_8_out, not_9_out, not_10_out, not_11_out, not_12_out,
       not_13_out, not_14_out, not_15_out, not_16_out;

  and and_1 (carry_flag, and_2_out, not_1_out);
  not not_1 (not_1_out, \input [15]);
  and and_2 (and_2_out, and_3_out, not_2_out);
  not not_2 (not_2_out, \input [14]);
  xor xor_1 (\output [15], \input [15], and_2_out);
  and and_3 (and_3_out, and_4_out, not_3_out);
  not not_3 (not_3_out, \input [13]);
  xor xor_2 (\output [14], \input [14], and_3_out);
  and and_4 (and_4_out, and_5_out, not_4_out);
  xor xor_3 (\output [13], \input [13], and_4_out);
  and and_5 (and_5_out, and_6_out, not_5_out);
  not not_4 (not_4_out, \input [12]);
  xor xor_4 (\output [12], \input [12], and_5_out);
  and and_6 (and_6_out, and_7_out, not_6_out);
  not not_5 (not_5_out, \input [11]);
  xor xor_5 (\output [11], \input [11], and_6_out);
  not not_6 (not_6_out, \input [10]);
  xor xor_6 (\output [10], \input [10], and_7_out);
  and and_7 (and_7_out, and_8_out, not_7_out);
  not not_7 (not_7_out, \input [9]);
  xor xor_7 (\output [9], \input [9], and_8_out);
  and and_8 (and_8_out, and_9_out, not_8_out);
  not not_8 (not_8_out, \input [8]);
  and and_9 (and_9_out, and_10_out, not_9_out);
  not not_9 (not_9_out, \input [7]);
  xor xor_8 (\output [8], \input [8], and_9_out);
  and and_10 (and_10_out, and_11_out, not_10_out);
  not not_10 (not_10_out, \input [6]);
  xor xor_9 (\output [7], \input [7], and_10_out);
  and and_11 (and_11_out, and_12_out, not_11_out);
  not not_11 (not_11_out, \input [5]);
  xor xor_10 (\output [6], \input [6], and_11_out);
  and and_12 (and_12_out, and_13_out, not_12_out);
  xor xor_11 (\output [5], \input [5], and_12_out);
  and and_13 (and_13_out, and_14_out, not_13_out);
  not not_12 (not_12_out, \input [4]);
  xor xor_12 (\output [4], \input [4], and_13_out);
  and and_14 (and_14_out, and_15_out, not_14_out);
  not not_13 (not_13_out, \input [3]);
  xor xor_13 (\output [3], \input [3], and_14_out);
  not not_14 (not_14_out, \input [2]);
  xor xor_14 (\output [2], \input [2], and_15_out);
  and and_15 (and_15_out, \output [0], not_15_out);
  not not_15 (not_15_out, \input [1]);
  xor xor_15 (\output [1], \input [1], \output [0]);
  and and_16 (\output [0], not_16_out, 1'b1);
  not not_16 (not_16_out, \input [0]);
endmodule

module ALU (
  input  [15:0] input2,
  input  [15:0] input1,
  input  [2:0] control_inp_2,
  input  [2:0] Control_inpt,
  output [15:0] aluoutput,
  output zero_flag
);

  wire and_1_out;
  wire [15:0] adder_1_out, and_16_bits_1_result, decrementer_1_output, inc_16_bits_1_output,
       multiplexer_1_out, multiplexer_3_out, not_16_bits_1_out_2, or_16_bits_1_result, subtractor_1_result,
       xor_16_bits_1_result;

  Decrementer decrementer_1 (.\input (input1), .\output (decrementer_1_output));  // open: carry_flag
  Inc_16_bits inc_16_bits_1 (.\input (input1), .\output (inc_16_bits_1_output));  // open: carry
  Not_16_bits not_16_bits_1 (.in_1(input1), .out_2(not_16_bits_1_out_2));
  Multiplexer #(.select(3), .width(16)) multiplexer_1 (
    .in0(not_16_bits_1_out_2), .in1(input1), .in2(inc_16_bits_1_output), .in3(decrementer_1_output),
    .in4({16{1'b0}}), .in5({16{1'b0}}), .in6({16{1'b0}}), .in7({16{1'b0}}), .out(multiplexer_1_out),
    .sel(control_inp_2));  // open: en
  and and_1 (and_1_out, Control_inpt[0], Control_inpt[1], Control_inpt[2]);
  Xor_16_bits xor_16_bits_1 (.a(input2), .b(input1), .result(xor_16_bits_1_result));
  Multiplexer #(.width(16)) multiplexer_2 (
    .in0(multiplexer_3_out), .in1(multiplexer_1_out), .out(aluoutput), .sel(and_1_out));  // open: en
  Or_16_bits or_16_bits_1 (.a(input2), .b(input1), .result(or_16_bits_1_result));
  And_16_bits and_16_bits_1 (.a(input2), .b(input1), .result(and_16_bits_1_result));
  Subtractor subtractor_1 (.ai(input2), .bi(input1), .result(subtractor_1_result));  // open: carry
  Multiplexer #(.select(3), .width(16)) multiplexer_3 (
    .in0(adder_1_out), .in1(subtractor_1_result), .in2(and_16_bits_1_result), .in3(or_16_bits_1_result),
    .in4(xor_16_bits_1_result), .out(multiplexer_3_out), .sel(Control_inpt));  // open: in5, in6, in7, en
  nor nor_1 (zero_flag, aluoutput[15], aluoutput[14], aluoutput[13], aluoutput[12], aluoutput[11], aluoutput[10], aluoutput[9], aluoutput[8], aluoutput[7], aluoutput[6], aluoutput[5], aluoutput[4], aluoutput[3], aluoutput[2], aluoutput[1], aluoutput[0]);
  Adder_part #(.width(16)) adder_1 (.a(input1), .b(input2), .out(adder_1_out));  // open: cin, cout
endmodule

module myRegister (
  input  reset,
  input  [15:0] \input ,
  input  ld,
  input  clock,
  output [15:0] \output 
);

  wire and_1_out, and_2_out, and_3_out, and_4_out, and_5_out, and_6_out, and_7_out, and_8_out, and_9_out,
       and_10_out, and_11_out, and_12_out, and_13_out, and_14_out, and_15_out, and_16_out, and_17_out,
       and_18_out, and_19_out, and_20_out, and_21_out, and_22_out, and_23_out, and_24_out, and_25_out,
       and_26_out, and_27_out, and_28_out, and_29_out, and_30_out, and_31_out, and_32_out, not_1_out,
       not_2_out, not_3_out, not_4_out, not_5_out, not_6_out, not_7_out, not_8_out, not_9_out, not_10_out,
       not_11_out, not_12_out, not_13_out, not_14_out, not_15_out, not_16_out;

  not not_1 (not_1_out, \input [0]);
  not not_2 (not_2_out, \input [1]);
  not not_3 (not_3_out, \input [2]);
  not not_4 (not_4_out, \input [3]);
  not not_5 (not_5_out, \input [4]);
  not not_6 (not_6_out, \input [5]);
  not not_7 (not_7_out, \input [6]);
  not not_8 (not_8_out, \input [7]);
  not not_9 (not_9_out, \input [8]);
  not not_10 (not_10_out, \input [9]);
  not not_11 (not_11_out, \input [10]);
  not not_12 (not_12_out, \input [11]);
  not not_13 (not_13_out, \input [12]);
  not not_14 (not_14_out, \input [13]);
  not not_15 (not_15_out, \input [14]);
  not not_16 (not_16_out, \input [15]);
  and and_1 (and_1_out, \input [0], ld);
  and and_2 (and_2_out, not_1_out, ld);
  and and_3 (and_3_out, \input [1], ld);
  and and_4 (and_4_out, not_2_out, ld);
  and and_5 (and_5_out, \input [2], ld);
  and and_6 (and_6_out, not_3_out, ld);
  and and_7 (and_7_out, \input [3], ld);
  and and_8 (and_8_out, not_4_out, ld);
  and and_9 (and_9_out, \input [4], ld);
  and and_10 (and_10_out, not_5_out, ld);
  and and_11 (and_11_out, \input [5], ld);
  and and_12 (and_12_out, not_6_out, ld);
  and and_13 (and_13_out, \input [6], ld);
  and and_14 (and_14_out, not_7_out, ld);
  and and_15 (and_15_out, \input [7], ld);
  and and_16 (and_16_out, not_8_out, ld);
  and and_17 (and_17_out, \input [8], ld);
  and and_18 (and_18_out, not_9_out, ld);
  and and_19 (and_19_out, \input [9], ld);
  and and_20 (and_20_out, not_10_out, ld);
  and and_21 (and_21_out, \input [10], ld);
  and and_22 (and_22_out, not_11_out, ld);
  and and_23 (and_23_out, \input [11], ld);
  and and_24 (and_24_out, not_12_out, ld);
  and and_25 (and_25_out, \input [12], ld);
  and and_26 (and_26_out, not_13_out, ld);
  and and_27 (and_27_out, \input [13], ld);
  and and_28 (and_28_out, not_14_out, ld);
  and and_29 (and_29_out, \input [14], ld);
  and and_30 (and_30_out, not_15_out, ld);
  and and_31 (and_31_out, \input [15], ld);
  and and_32 (and_32_out, not_16_out, ld);
  S_R_Flip_Flop s_r_ff_1 (
    .S(and_1_out), .clk(clock), .R(and_2_out), .Q(\output [0]), .reset(reset));  // open: Qn, preset, en
  S_R_Flip_Flop s_r_ff_2 (
    .S(and_3_out), .clk(clock), .R(and_4_out), .Q(\output [1]), .reset(reset));  // open: Qn, preset, en
  S_R_Flip_Flop s_r_ff_3 (
    .S(and_5_out), .clk(clock), .R(and_6_out), .Q(\output [2]), .reset(reset));  // open: Qn, preset, en
  S_R_Flip_Flop s_r_ff_4 (
    .S(and_7_out), .clk(clock), .R(and_8_out), .Q(\output [3]), .reset(reset));  // open: Qn, preset, en
  S_R_Flip_Flop s_r_ff_5 (
    .S(and_9_out), .clk(clock), .R(and_10_out), .Q(\output [4]), .reset(reset));  // open: Qn, preset, en
  S_R_Flip_Flop s_r_ff_6 (
    .S(and_11_out), .clk(clock), .R(and_12_out), .Q(\output [5]), .reset(reset));  // open: Qn, preset, en
  S_R_Flip_Flop s_r_ff_7 (
    .S(and_13_out), .clk(clock), .R(and_14_out), .Q(\output [6]), .reset(reset));  // open: Qn, preset, en
  S_R_Flip_Flop s_r_ff_8 (
    .S(and_15_out), .clk(clock), .R(and_16_out), .Q(\output [7]), .reset(reset));  // open: Qn, preset, en
  S_R_Flip_Flop s_r_ff_9 (
    .S(and_17_out), .clk(clock), .R(and_18_out), .Q(\output [8]), .reset(reset));  // open: Qn, preset, en
  S_R_Flip_Flop s_r_ff_10 (
    .S(and_19_out), .clk(clock), .R(and_20_out), .Q(\output [9]), .reset(reset));  // open: Qn, preset, en
  S_R_Flip_Flop s_r_ff_11 (
    .S(and_21_out), .clk(clock), .R(and_22_out), .Q(\output [10]), .reset(reset));  // open: Qn, preset, en
  S_R_Flip_Flop s_r_ff_12 (
    .S(and_23_out), .clk(clock), .R(and_24_out), .Q(\output [11]), .reset(reset));  // open: Qn, preset, en
  S_R_Flip_Flop s_r_ff_13 (
    .S(and_25_out), .clk(clock), .R(and_26_out), .Q(\output [12]), .reset(reset));  // open: Qn, preset, en
  S_R_Flip_Flop s_r_ff_14 (
    .S(and_27_out), .clk(clock), .R(and_28_out), .Q(\output [13]), .reset(reset));  // open: Qn, preset, en
  S_R_Flip_Flop s_r_ff_15 (
    .S(and_29_out), .clk(clock), .R(and_30_out), .Q(\output [14]), .reset(reset));  // open: Qn, preset, en
  S_R_Flip_Flop s_r_ff_16 (
    .S(and_31_out), .clk(clock), .R(and_32_out), .Q(\output [15]), .reset(reset));  // open: Qn, preset, en
endmodule

module pcReg (
  input  inc,
  input  [11:0] \input ,
  input  load,
  input  clock,
  output [11:0] \output ,
  output cOut
);

  wire and_1_out, and_2_out, and_3_out, and_4_out, and_5_out, and_6_out, and_7_out, and_8_out, and_9_out,
       and_10_out, and_11_out, and_12_out, and_13_out, and_14_out, and_15_out, and_16_out, and_17_out,
       and_18_out, and_19_out, and_20_out, and_21_out, and_22_out, and_23_out, and_24_out, and_25_out,
       and_26_out, and_27_out, and_28_out, and_29_out, and_30_out, and_31_out, and_33_out, and_34_out,
       and_35_out, and_36_out, and_37_out, and_38_out, and_39_out, and_40_out, and_41_out, and_42_out,
       and_43_out, and_44_out, and_45_out, and_46_out, and_47_out, and_48_out, and_49_out, and_50_out,
       and_51_out, and_52_out, and_53_out, and_54_out, and_55_out, and_56_out, and_57_out, and_58_out,
       and_59_out, and_60_out, not_1_out, not_2_out, not_3_out, not_4_out, not_5_out, not_6_out, not_7_out,
       not_8_out, not_9_out, not_10_out, not_11_out, not_12_out, not_13_out, not_14_out, not_15_out,
       not_16_out, not_17_out, not_18_out, not_19_out, not_20_out, not_21_out, not_22_out, not_23_out,
       not_24_out, or_1_out, or_2_out, or_3_out, or_4_out, or_5_out, or_6_out, or_7_out, or_8_out, or_9_out,
       or_10_out, or_11_out, or_12_out, or_13_out, or_14_out, or_15_out, or_16_out, or_17_out, or_18_out,
       or_19_out, or_20_out, or_21_out, or_22_out, or_23_out, or_24_out, xor_1_out, xor_2_out, xor_3_out,
       xor_4_out, xor_5_out, xor_6_out, xor_7_out, xor_8_out, xor_9_out, xor_10_out, xor_11_out, xor_12_out;

  and and_1 (and_1_out, \input [0], load);
  and and_2 (and_2_out, load, not_1_out);
  not not_1 (not_1_out, \input [0]);
  and and_3 (and_3_out, \input [1], load);
  and and_4 (and_4_out, load, not_2_out);
  not not_2 (not_2_out, \input [1]);
  and and_5 (and_5_out, \input [2], load);
  and and_6 (and_6_out, load, not_3_out);
  not not_3 (not_3_out, \input [2]);
  and and_7 (and_7_out, \input [3], load);
  and and_8 (and_8_out, load, not_4_out);
  not not_4 (not_4_out, \input [3]);
  and and_9 (and_9_out, \input [4], load);
  and and_10 (and_10_out, load, not_5_out);
  not not_5 (not_5_out, \input [4]);
  and and_11 (and_11_out, \input [5], load);
  and and_12 (and_12_out, load, not_6_out);
  not not_6 (not_6_out, \input [5]);
  and and_13 (and_13_out, \input [6], load);
  and and_14 (and_14_out, load, not_7_out);
  not not_7 (not_7_out, \input [6]);
  and and_15 (and_15_out, \input [7], load);
  and and_16 (and_16_out, load, not_8_out);
  not not_8 (not_8_out, \input [7]);
  and and_17 (and_17_out, \input [8], load);
  and and_18 (and_18_out, load, not_9_out);
  not not_9 (not_9_out, \input [8]);
  and and_19 (and_19_out, \input [9], load);
  and and_20 (and_20_out, load, not_10_out);
  not not_10 (not_10_out, \input [9]);
  and and_21 (and_21_out, \input [10], load);
  and and_22 (and_22_out, load, not_11_out);
  not not_11 (not_11_out, \input [10]);
  and and_23 (and_23_out, \input [11], load);
  and and_24 (and_24_out, load, not_12_out);
  not not_12 (not_12_out, \input [11]);
  xor xor_1 (xor_1_out, inc, \output [0]);
  xor xor_2 (xor_2_out, and_33_out, \output [1]);
  xor xor_3 (xor_3_out, and_34_out, \output [2]);
  xor xor_4 (xor_4_out, and_37_out, \output [3]);
  xor xor_5 (xor_5_out, and_38_out, \output [4]);
  and and_25 (and_25_out, and_38_out, \output [4]);
  xor xor_6 (xor_6_out, and_25_out, \output [5]);
  and and_26 (and_26_out, and_25_out, \output [5]);
  and and_27 (and_27_out, and_26_out, \output [6]);
  xor xor_7 (xor_7_out, and_26_out, \output [6]);
  and and_28 (and_28_out, and_27_out, \output [7]);
  xor xor_8 (xor_8_out, and_27_out, \output [7]);
  and and_29 (and_29_out, and_28_out, \output [8]);
  xor xor_9 (xor_9_out, and_28_out, \output [8]);
  and and_30 (and_30_out, and_29_out, \output [9]);
  xor xor_10 (xor_10_out, and_29_out, \output [9]);
  and and_31 (and_31_out, and_30_out, \output [10]);
  xor xor_11 (xor_11_out, and_30_out, \output [10]);
  buf and_32 (cOut, and_31_out);  // AND_Gate
  xor xor_12 (xor_12_out, and_31_out, \output [11]);
  and and_33 (and_33_out, inc, \output [0]);
  not not_13 (not_13_out, xor_1_out);
  and and_34 (and_34_out, and_33_out, \output [1]);
  and and_35 (and_35_out, xor_2_out, inc);
  and and_36 (and_36_out, inc, not_14_out);
  not not_14 (not_14_out, xor_2_out);
  and and_37 (and_37_out, and_34_out, \output [2]);
  not not_15 (not_15_out, xor_3_out);
  and and_38 (and_38_out, and_37_out, \output [3]);
  not not_16 (not_16_out, xor_4_out);
  and and_39 (and_39_out, xor_5_out, inc);
  and and_40 (and_40_out, inc, not_17_out);
  not not_17 (not_17_out, xor_5_out);
  and and_41 (and_41_out, xor_6_out, inc);
  and and_42 (and_42_out, inc, not_18_out);
  not not_18 (not_18_out, xor_6_out);
  and and_43 (and_43_out, xor_7_out, inc);
  and and_44 (and_44_out, inc, not_19_out);
  not not_19 (not_19_out, xor_7_out);
  and and_45 (and_45_out, xor_8_out, inc);
  and and_46 (and_46_out, inc, not_20_out);
  not not_20 (not_20_out, xor_8_out);
  and and_47 (and_47_out, xor_9_out, inc);
  and and_48 (and_48_out, inc, not_21_out);
  not not_21 (not_21_out, xor_9_out);
  and and_49 (and_49_out, xor_10_out, inc);
  and and_50 (and_50_out, inc, not_22_out);
  not not_22 (not_22_out, xor_10_out);
  and and_51 (and_51_out, xor_11_out, inc);
  and and_52 (and_52_out, inc, not_23_out);
  not not_23 (not_23_out, xor_11_out);
  and and_53 (and_53_out, xor_12_out, inc);
  and and_54 (and_54_out, inc, not_24_out);
  not not_24 (not_24_out, xor_12_out);
  and and_55 (and_55_out, xor_1_out, inc);
  and and_56 (and_56_out, inc, not_13_out);
  and and_57 (and_57_out, xor_3_out, inc);
  and and_58 (and_58_out, inc, not_15_out);
  and and_59 (and_59_out, xor_4_out, inc);
  and and_60 (and_60_out, inc, not_16_out);
  or or_1 (or_1_out, and_1_out, and_55_out);
  or or_2 (or_2_out, and_56_out, and_2_out);
  or or_3 (or_3_out, and_3_out, and_35_out);
  or or_4 (or_4_out, and_4_out, and_36_out);
  or or_5 (or_5_out, and_5_out, and_57_out);
  or or_6 (or_6_out, and_6_out, and_58_out);
  or or_7 (or_7_out, and_7_out, and_59_out);
  or or_8 (or_8_out, and_8_out, and_60_out);
  or or_9 (or_9_out, and_9_out, and_39_out);
  or or_10 (or_10_out, and_10_out, and_40_out);
  or or_11 (or_11_out, and_11_out, and_41_out);
  or or_12 (or_12_out, and_12_out, and_42_out);
  or or_13 (or_13_out, and_13_out, and_43_out);
  or or_14 (or_14_out, and_14_out, and_44_out);
  or or_15 (or_15_out, and_15_out, and_45_out);
  or or_16 (or_16_out, and_16_out, and_46_out);
  or or_17 (or_17_out, and_17_out, and_47_out);
  or or_18 (or_18_out, and_18_out, and_48_out);
  or or_19 (or_19_out, and_19_out, and_49_out);
  or or_20 (or_20_out, and_20_out, and_50_out);
  or or_21 (or_21_out, and_21_out, and_51_out);
  or or_22 (or_22_out, and_22_out, and_52_out);
  or or_23 (or_23_out, and_23_out, and_53_out);
  or or_24 (or_24_out, and_24_out, and_54_out);
  S_R_Flip_Flop s_r_ff_1 (.S(or_1_out), .clk(clock), .R(or_2_out), .Q(\output [0]));  // open: Qn, preset, reset, en
  S_R_Flip_Flop s_r_ff_2 (.S(or_3_out), .clk(clock), .R(or_4_out), .Q(\output [1]));  // open: Qn, preset, reset, en
  S_R_Flip_Flop s_r_ff_3 (.S(or_5_out), .clk(clock), .R(or_6_out), .Q(\output [2]));  // open: Qn, preset, reset, en
  S_R_Flip_Flop s_r_ff_4 (.S(or_7_out), .clk(clock), .R(or_8_out), .Q(\output [3]));  // open: Qn, preset, reset, en
  S_R_Flip_Flop s_r_ff_5 (.S(or_9_out), .clk(clock), .R(or_10_out), .Q(\output [4]));  // open: Qn, preset, reset, en
  S_R_Flip_Flop s_r_ff_6 (.S(or_11_out), .clk(clock), .R(or_12_out), .Q(\output [5]));  // open: Qn, preset, reset, en
  S_R_Flip_Flop s_r_ff_7 (.S(or_13_out), .clk(clock), .R(or_14_out), .Q(\output [6]));  // open: Qn, preset, reset, en
  S_R_Flip_Flop s_r_ff_8 (.S(or_15_out), .clk(clock), .R(or_16_out), .Q(\output [7]));  // open: Qn, preset, reset, en
  S_R_Flip_Flop s_r_ff_9 (.S(or_17_out), .clk(clock), .R(or_18_out), .Q(\output [8]));  // open: Qn, preset, reset, en
  S_R_Flip_Flop s_r_ff_10 (.S(or_19_out), .clk(clock), .R(or_20_out), .Q(\output [9]));  // open: Qn, preset, reset, en
  S_R_Flip_Flop s_r_ff_11 (.S(or_21_out), .clk(clock), .R(or_22_out), .Q(\output [10]));  // open: Qn, preset, reset, en
  S_R_Flip_Flop s_r_ff_12 (.S(or_23_out), .clk(clock), .R(or_24_out), .Q(\output [11]));  // open: Qn, preset, reset, en
endmodule

module \REGİSTER__BANK  (
  input  SP_plus_plus,
  input  SP_minus_minus,
  input  CLI,
  input  STI,
  input  ZfLoad_Ctrl,
  input  Zf_ALU,
  input  flagld,
  input  RegBankLd,
  input  [2:0] RegSelect,
  input  clock,
  input  [15:0] RegBankInp,
  output [15:0] out_12,
  output [15:0] out_13,
  output [15:0] out_14,
  output [15:0] out_15,
  output [15:0] out_16,
  output [15:0] out_17,
  output [15:0] out_18,
  output [15:0] out_19
);

  wire and_1_out, and_2_out, and_3_out, and_4_out, and_5_out, and_6_out, and_7_out, and_8_out,
       decoder_1_out0, decoder_1_out1, decoder_1_out2, decoder_1_out3, decoder_1_out4, decoder_1_out5,
       decoder_1_out6, decoder_1_out7, or_1_out;

  Decoder #(.select(3)) decoder_1 (
    .out0(decoder_1_out0), .out1(decoder_1_out1), .out2(decoder_1_out2), .out3(decoder_1_out3),
    .out4(decoder_1_out4), .out5(decoder_1_out5), .out6(decoder_1_out6), .out7(decoder_1_out7),
    .sel(RegSelect));  // open: en
  and and_1 (and_1_out, RegBankLd, decoder_1_out0);
  and and_2 (and_2_out, RegBankLd, decoder_1_out1);
  and and_3 (and_3_out, RegBankLd, decoder_1_out2);
  and and_4 (and_4_out, RegBankLd, decoder_1_out3);
  and and_5 (and_5_out, RegBankLd, decoder_1_out4);
  and and_6 (and_6_out, RegBankLd, decoder_1_out5);
  regSti regsti_1 (
    .\input (RegBankInp), .CLI(CLI), .STI(STI), .ZfLoad_Ctrl(ZfLoad_Ctrl), .Zf_ALU(Zf_ALU), .ld(or_1_out),
    .clock(clock), .\output (out_18));  // open: reset
  and and_7 (and_7_out, RegBankLd, decoder_1_out6);
  or or_1 (or_1_out, and_7_out, flagld);
  and and_8 (and_8_out, RegBankLd, decoder_1_out7);
  myRegister myregister_1 (.\input (RegBankInp), .ld(and_1_out), .clock(clock), .\output (out_12));  // open: reset
  myRegister myregister_2 (.\input (RegBankInp), .ld(and_2_out), .clock(clock), .\output (out_13));  // open: reset
  myRegister myregister_3 (.\input (RegBankInp), .ld(and_3_out), .clock(clock), .\output (out_14));  // open: reset
  myRegister myregister_4 (.\input (RegBankInp), .ld(and_4_out), .clock(clock), .\output (out_15));  // open: reset
  myRegister myregister_5 (.\input (RegBankInp), .ld(and_5_out), .clock(clock), .\output (out_16));  // open: reset
  myRegister myregister_6 (.\input (RegBankInp), .ld(and_6_out), .clock(clock), .\output (out_17));  // open: reset
  register7 register7_1 (
    .\input (RegBankInp), .SP_plus_plus(SP_plus_plus), .SP_minus_minus(SP_minus_minus), .ld(and_8_out),
    .clock(clock), .\output (out_19));
endmodule

module Control_Unit (
  input  [3:0] Opcode,
  input  ZfFlag_regbank,
  input  int_flag_regBank,
  input  \int ,
  input  clk,
  output SP_minus_minus,
  output SP_plus_plus,
  output irLd,
  output MemLd,
  output mux0,
  output mux1,
  output next,
  output zf_ld,
  output regLd,
  output ArMux0,
  output ArMux1,
  output PC_plus_plus,
  output PcLd,
  output ret,
  output Cli,
  output Sti,
  output flagld,
  output intld,
  output intach,
  output PC_minus_minus
);

  wire and_1_out, and_2_out, and_3_out;
  wire [5:0] multiplexer_1_out, multiplexer_2_out, multiplexer_3_out, multiplexer_4_out, n6bitreg2_1_output;
  wire [27:0] rom_1_data;

  _6bitreg2 u_6bitreg2_1 (.\input (multiplexer_4_out), .\output (n6bitreg2_1_output), .clk(clk));
  and and_1 (and_1_out, ~Opcode[0], ~Opcode[1], Opcode[2], ~Opcode[3]);  // AND_Gate
  Multiplexer #(.width(6), .enable("false")) multiplexer_1 (
    .in0({6{1'b0}}), .in1(6'b001010), .out(multiplexer_1_out), .sel(ZfFlag_regbank));
  Multiplexer #(.width(6), .enable("false")) multiplexer_2 (
    .in0({1'b0, Opcode, 1'b0}), .in1(multiplexer_1_out), .out(multiplexer_2_out), .sel(and_1_out));
  Multiplexer #(.width(6), .enable("false")) multiplexer_3 (
    .in0(rom_1_data[5:0]), .in1(multiplexer_2_out), .out(multiplexer_3_out), .sel(rom_1_data[25]));
  Multiplexer #(.width(6), .enable("false")) multiplexer_4 (
    .in0(multiplexer_3_out), .in1(6'b011111), .out(multiplexer_4_out), .sel(and_2_out));
  ROM #(.addrWidth(6), .dataWidth(28)) rom_1 (
    .addr(n6bitreg2_1_output),
    .data({rom_1_data[27:25], flagld, ArMux1, ArMux0, irLd, MemLd, next, mux1, mux0, PC_plus_plus, PcLd, regLd, ret, SP_plus_plus, SP_minus_minus, zf_ld, Cli, Sti, intach, intld, rom_1_data[5:0]}),
    .sel(1'b1));
  and and_2 (and_2_out, and_3_out, int_flag_regBank, \int );
  and and_3 (and_3_out, ~rom_1_data[0], ~rom_1_data[1], ~rom_1_data[2], ~rom_1_data[3], ~rom_1_data[4], ~rom_1_data[5]);  // AND_Gate

  assign PC_minus_minus = 1'b0;

  // Notes on the sheet:
  //   contents of rom_1 (hex, n*v repeats v):
  //   221003f 0 14000 0 404000 0 520000 0 0 0 8000 0 0 0 64400 0 920800 0 1013 804000 988800 0 1017 80a000
  //   100 0 2000201 0 101d 80b01e 1804000 a0820 9809e1 2c0a001
endmodule

module _4_bit_Reg (
  input  [3:0] \input ,
  input  clock,
  output [3:0] \output 
);

  wire and_1_out, and_2_out, and_3_out, and_4_out, and_5_out, and_6_out, and_7_out, and_8_out, not_1_out,
       not_2_out, not_3_out, not_4_out;

  not not_1 (not_1_out, \input [0]);
  not not_2 (not_2_out, \input [1]);
  not not_3 (not_3_out, \input [2]);
  not not_4 (not_4_out, \input [3]);
  and and_1 (and_1_out, \input [0], 1'b1);
  and and_2 (and_2_out, not_1_out, 1'b1);
  and and_3 (and_3_out, \input [1], 1'b1);
  and and_4 (and_4_out, not_2_out, 1'b1);
  and and_5 (and_5_out, \input [2], 1'b1);
  and and_6 (and_6_out, not_3_out, 1'b1);
  and and_7 (and_7_out, \input [3], 1'b1);
  and and_8 (and_8_out, not_4_out, 1'b1);
  S_R_Flip_Flop s_r_ff_1 (.S(and_1_out), .clk(clock), .R(and_2_out), .Q(\output [0]));  // open: Qn, preset, reset, en
  S_R_Flip_Flop s_r_ff_2 (.S(and_3_out), .clk(clock), .R(and_4_out), .Q(\output [1]));  // open: Qn, preset, reset, en
  S_R_Flip_Flop s_r_ff_3 (.S(and_5_out), .clk(clock), .R(and_6_out), .Q(\output [2]));  // open: Qn, preset, reset, en
  S_R_Flip_Flop s_r_ff_4 (.S(and_7_out), .clk(clock), .R(and_8_out), .Q(\output [3]));  // open: Qn, preset, reset, en
endmodule

module ZF_reg (
  input  inp,
  input  ZFld,
  input  clock,
  output out
);

  wire and_1_out, and_2_out, not_1_out;

  not not_1 (not_1_out, inp);
  and and_1 (and_1_out, inp, ZFld);
  and and_2 (and_2_out, not_1_out, ZFld);
  S_R_Flip_Flop s_r_ff_1 (.S(and_1_out), .clk(clock), .R(and_2_out), .Q(out));  // open: Qn, preset, reset, en
endmodule

module register7 (
  input  SP_plus_plus,
  input  SP_minus_minus,
  input  [15:0] \input ,
  input  clock,
  input  ld,
  output [15:0] \output 
);

  wire and_1_out, and_2_out, and_3_out, and_4_out, and_5_out, and_6_out, and_7_out, and_8_out, and_9_out,
       and_10_out, and_11_out, and_12_out, and_13_out, and_14_out, and_15_out, and_16_out, and_17_out,
       and_18_out, and_19_out, and_20_out, and_21_out, and_22_out, and_23_out, and_24_out, and_25_out,
       and_26_out, and_27_out, and_28_out, and_29_out, and_30_out, and_31_out, and_32_out, and_33_out,
       and_34_out, and_35_out, and_36_out, and_37_out, and_38_out, and_39_out, and_40_out, and_41_out,
       and_42_out, and_43_out, and_44_out, and_45_out, and_46_out, and_47_out, and_48_out, and_49_out,
       and_50_out, and_51_out, and_52_out, and_53_out, and_54_out, and_55_out, and_56_out, and_57_out,
       and_58_out, and_59_out, and_60_out, and_61_out, and_62_out, and_63_out, and_64_out, and_65_out,
       and_67_out, and_68_out, and_69_out, and_70_out, and_71_out, and_72_out, and_73_out, and_74_out,
       and_75_out, and_76_out, and_77_out, and_78_out, and_79_out, and_80_out, and_81_out, and_82_out,
       and_83_out, and_84_out, and_85_out, and_86_out, and_87_out, and_88_out, and_89_out, and_90_out,
       and_91_out, and_92_out, and_93_out, and_94_out, and_95_out, and_96_out, and_97_out, and_98_out,
       and_99_out, and_100_out, and_101_out, and_103_out, and_104_out, not_1_out, not_2_out, not_3_out,
       not_4_out, not_5_out, not_6_out, not_7_out, not_8_out, not_9_out, not_10_out, not_11_out, not_12_out,
       not_13_out, not_14_out, not_15_out, not_16_out, not_17_out, not_18_out, not_19_out, not_20_out,
       not_21_out, not_22_out, not_23_out, not_24_out, not_25_out, not_26_out, not_27_out, not_28_out,
       not_29_out, not_30_out, not_31_out, not_32_out, not_33_out, not_34_out, not_35_out, not_36_out,
       not_37_out, not_38_out, not_39_out, not_40_out, not_41_out, not_42_out, not_43_out, not_44_out,
       not_45_out, not_46_out, not_47_out, not_48_out, not_49_out, not_50_out, not_51_out, not_52_out,
       or_1_out, or_2_out, or_3_out, or_4_out, or_5_out, or_6_out, or_7_out, or_8_out, or_9_out, or_10_out,
       or_11_out, or_12_out, or_13_out, or_14_out, or_15_out, or_16_out, or_17_out, or_18_out, or_19_out,
       or_20_out, or_21_out, or_22_out, or_23_out, or_24_out, xor_1_out, xor_2_out, xor_3_out, xor_4_out,
       xor_5_out, xor_6_out, xor_7_out, xor_8_out, xor_9_out, xor_10_out, xor_11_out, xor_12_out, xor_13_out,
       xor_14_out, xor_15_out, xor_16_out, xor_17_out, xor_18_out, xor_19_out, xor_20_out, xor_21_out,
       xor_22_out, xor_23_out;

  and and_1 (and_1_out, \input [0], ld);
  not not_1 (not_1_out, \input [0]);
  and and_2 (and_2_out, not_1_out, ld);
  and and_3 (and_3_out, \input [1], ld);
  not not_2 (not_2_out, \input [1]);
  and and_4 (and_4_out, not_2_out, ld);
  and and_5 (and_5_out, \input [2], ld);
  not not_3 (not_3_out, \input [2]);
  and and_6 (and_6_out, not_3_out, ld);
  and and_7 (and_7_out, \input [3], ld);
  not not_4 (not_4_out, \input [3]);
  and and_8 (and_8_out, not_4_out, ld);
  and and_9 (and_9_out, \input [4], ld);
  not not_5 (not_5_out, \input [4]);
  and and_10 (and_10_out, not_5_out, ld);
  and and_11 (and_11_out, \input [5], ld);
  not not_6 (not_6_out, \input [5]);
  and and_12 (and_12_out, not_6_out, ld);
  and and_13 (and_13_out, \input [6], ld);
  not not_7 (not_7_out, \input [6]);
  and and_14 (and_14_out, not_7_out, ld);
  and and_15 (and_15_out, \input [7], ld);
  not not_8 (not_8_out, \input [7]);
  and and_16 (and_16_out, not_8_out, ld);
  and and_17 (and_17_out, \input [8], ld);
  not not_9 (not_9_out, \input [8]);
  and and_18 (and_18_out, not_9_out, ld);
  and and_19 (and_19_out, \input [9], ld);
  not not_10 (not_10_out, \input [9]);
  and and_20 (and_20_out, not_10_out, ld);
  and and_21 (and_21_out, \input [10], ld);
  not not_11 (not_11_out, \input [10]);
  and and_22 (and_22_out, not_11_out, ld);
  and and_23 (and_23_out, \input [11], ld);
  not not_12 (not_12_out, \input [11]);
  and and_24 (and_24_out, not_12_out, ld);
  and and_25 (and_25_out, \input [12], ld);
  not not_13 (not_13_out, \input [12]);
  and and_26 (and_26_out, not_13_out, ld);
  and and_27 (and_27_out, \input [13], ld);
  not not_14 (not_14_out, \input [13]);
  and and_28 (and_28_out, not_14_out, ld);
  and and_29 (and_29_out, \input [14], ld);
  not not_15 (not_15_out, \input [14]);
  and and_30 (and_30_out, not_15_out, ld);
  and and_31 (and_31_out, \input [15], ld);
  not not_16 (not_16_out, \input [15]);
  and and_32 (and_32_out, not_16_out, ld);
  xor xor_1 (xor_1_out, SP_plus_plus, \output [0]);
  not not_17 (not_17_out, xor_1_out);
  xor xor_2 (xor_2_out, and_33_out, \output [1]);
  not not_18 (not_18_out, xor_2_out);
  xor xor_3 (xor_3_out, and_36_out, \output [2]);
  not not_19 (not_19_out, xor_3_out);
  xor xor_4 (xor_4_out, and_39_out, \output [3]);
  not not_20 (not_20_out, xor_4_out);
  xor xor_5 (xor_5_out, and_42_out, \output [4]);
  not not_21 (not_21_out, xor_5_out);
  xor xor_6 (xor_6_out, and_45_out, \output [5]);
  not not_22 (not_22_out, xor_6_out);
  xor xor_7 (xor_7_out, and_48_out, \output [6]);
  not not_23 (not_23_out, xor_7_out);
  xor xor_8 (xor_8_out, and_51_out, \output [7]);
  not not_24 (not_24_out, xor_8_out);
  xor xor_9 (xor_9_out, and_54_out, \output [8]);
  not not_25 (not_25_out, xor_9_out);
  xor xor_10 (xor_10_out, and_57_out, \output [9]);
  not not_26 (not_26_out, xor_10_out);
  xor xor_11 (xor_11_out, and_60_out, \output [10]);
  not not_27 (not_27_out, xor_11_out);
  xor xor_12 (xor_12_out, and_63_out, \output [11]);
  not not_28 (not_28_out, xor_12_out);
  and and_33 (and_33_out, SP_plus_plus, \output [0]);
  and and_34 (and_34_out, xor_1_out, SP_plus_plus);
  and and_35 (and_35_out, not_17_out, SP_plus_plus);
  and and_36 (and_36_out, and_33_out, \output [1]);
  and and_37 (and_37_out, xor_2_out, SP_plus_plus);
  and and_38 (and_38_out, not_18_out, SP_plus_plus);
  and and_39 (and_39_out, and_36_out, \output [2]);
  and and_40 (and_40_out, xor_3_out, SP_plus_plus);
  and and_41 (and_41_out, not_19_out, SP_plus_plus);
  and and_42 (and_42_out, and_39_out, \output [3]);
  and and_43 (and_43_out, xor_4_out, SP_plus_plus);
  and and_44 (and_44_out, not_20_out, SP_plus_plus);
  and and_45 (and_45_out, and_42_out, \output [4]);
  and and_46 (and_46_out, xor_5_out, SP_plus_plus);
  and and_47 (and_47_out, not_21_out, SP_plus_plus);
  and and_48 (and_48_out, and_45_out, \output [5]);
  and and_49 (and_49_out, xor_6_out, SP_plus_plus);
  and and_50 (and_50_out, not_22_out, SP_plus_plus);
  and and_51 (and_51_out, and_48_out, \output [6]);
  and and_52 (and_52_out, xor_7_out, SP_plus_plus);
  and and_53 (and_53_out, not_23_out, SP_plus_plus);
  and and_54 (and_54_out, and_51_out, \output [7]);
  and and_55 (and_55_out, xor_8_out, SP_plus_plus);
  and and_56 (and_56_out, not_24_out, SP_plus_plus);
  and and_57 (and_57_out, and_54_out, \output [8]);
  and and_58 (and_58_out, xor_9_out, SP_plus_plus);
  and and_59 (and_59_out, not_25_out, SP_plus_plus);
  and and_60 (and_60_out, and_57_out, \output [9]);
  and and_61 (and_61_out, xor_10_out, SP_plus_plus);
  and and_62 (and_62_out, not_26_out, SP_plus_plus);
  and and_63 (and_63_out, and_60_out, \output [10]);
  and and_64 (and_64_out, xor_11_out, SP_plus_plus);
  and and_65 (and_65_out, not_27_out, SP_plus_plus);
  // AND_Gate and_66 has open pins: in0=and_63_out, in1=\output [11], out=open
  and and_67 (and_67_out, xor_12_out, SP_plus_plus);
  and and_68 (and_68_out, not_28_out, SP_plus_plus);
  and and_69 (and_69_out, SP_minus_minus, not_29_out);
  xor xor_13 (xor_13_out, and_69_out, \output [1]);
  xor xor_14 (xor_14_out, and_72_out, \output [2]);
  xor xor_15 (xor_15_out, and_75_out, \output [3]);
  xor xor_16 (xor_16_out, and_78_out, \output [4]);
  xor xor_17 (xor_17_out, and_81_out, \output [5]);
  xor xor_18 (xor_18_out, and_84_out, \output [6]);
  xor xor_19 (xor_19_out, and_87_out, \output [7]);
  xor xor_20 (xor_20_out, and_90_out, \output [8]);
  xor xor_21 (xor_21_out, and_93_out, \output [9]);
  xor xor_22 (xor_22_out, and_96_out, \output [10]);
  xor xor_23 (xor_23_out, and_99_out, \output [11]);
  not not_29 (not_29_out, \output [0]);
  and and_70 (and_70_out, and_69_out, SP_minus_minus);
  not not_30 (not_30_out, and_69_out);
  and and_71 (and_71_out, not_30_out, SP_minus_minus);
  not not_31 (not_31_out, \output [1]);
  and and_72 (and_72_out, and_69_out, not_31_out);
  and and_73 (and_73_out, xor_13_out, SP_minus_minus);
  not not_32 (not_32_out, xor_13_out);
  and and_74 (and_74_out, not_32_out, SP_minus_minus);
  not not_33 (not_33_out, \output [2]);
  and and_75 (and_75_out, and_72_out, not_33_out);
  and and_76 (and_76_out, xor_14_out, SP_minus_minus);
  not not_34 (not_34_out, xor_14_out);
  and and_77 (and_77_out, not_34_out, SP_minus_minus);
  not not_35 (not_35_out, \output [3]);
  and and_78 (and_78_out, and_75_out, not_35_out);
  and and_79 (and_79_out, xor_15_out, SP_minus_minus);
  not not_36 (not_36_out, xor_15_out);
  and and_80 (and_80_out, not_36_out, SP_minus_minus);
  not not_37 (not_37_out, \output [4]);
  and and_81 (and_81_out, and_78_out, not_37_out);
  and and_82 (and_82_out, xor_16_out, SP_minus_minus);
  not not_38 (not_38_out, xor_16_out);
  and and_83 (and_83_out, not_38_out, SP_minus_minus);
  not not_39 (not_39_out, \output [5]);
  and and_84 (and_84_out, and_81_out, not_39_out);
  and and_85 (and_85_out, xor_17_out, SP_minus_minus);
  not not_40 (not_40_out, xor_17_out);
  and and_86 (and_86_out, not_40_out, SP_minus_minus);
  not not_41 (not_41_out, \output [6]);
  and and_87 (and_87_out, and_84_out, not_41_out);
  and and_88 (and_88_out, xor_18_out, SP_minus_minus);
  not not_42 (not_42_out, xor_18_out);
  and and_89 (and_89_out, not_42_out, SP_minus_minus);
  not not_43 (not_43_out, \output [7]);
  and and_90 (and_90_out, and_87_out, not_43_out);
  and and_91 (and_91_out, xor_19_out, SP_minus_minus);
  not not_44 (not_44_out, xor_19_out);
  and and_92 (and_92_out, not_44_out, SP_minus_minus);
  not not_45 (not_45_out, \output [8]);
  and and_93 (and_93_out, and_90_out, not_45_out);
  and and_94 (and_94_out, xor_20_out, SP_minus_minus);
  not not_46 (not_46_out, xor_20_out);
  and and_95 (and_95_out, not_46_out, SP_minus_minus);
  not not_47 (not_47_out, \output [9]);
  and and_96 (and_96_out, and_93_out, not_47_out);
  and and_97 (and_97_out, xor_21_out, SP_minus_minus);
  not not_48 (not_48_out, xor_21_out);
  and and_98 (and_98_out, not_48_out, SP_minus_minus);
  not not_49 (not_49_out, \output [10]);
  and and_99 (and_99_out, and_96_out, not_49_out);
  and and_100 (and_100_out, xor_22_out, SP_minus_minus);
  not not_50 (not_50_out, xor_22_out);
  and and_101 (and_101_out, not_50_out, SP_minus_minus);
  not not_51 (not_51_out, \output [11]);
  // AND_Gate and_102 has open pins: in0=and_99_out, in1=not_51_out, out=open
  and and_103 (and_103_out, xor_23_out, SP_minus_minus);
  not not_52 (not_52_out, xor_23_out);
  and and_104 (and_104_out, not_52_out, SP_minus_minus);
  or or_1 (or_1_out, and_1_out, and_34_out, and_70_out);
  or or_2 (or_2_out, and_2_out, and_35_out, and_71_out);
  or or_3 (or_3_out, and_3_out, and_37_out, and_73_out);
  or or_4 (or_4_out, and_4_out, and_38_out, and_74_out);
  or or_5 (or_5_out, and_5_out, and_40_out, and_76_out);
  or or_6 (or_6_out, and_6_out, and_41_out, and_77_out);
  or or_7 (or_7_out, and_7_out, and_43_out, and_79_out);
  or or_8 (or_8_out, and_8_out, and_44_out, and_80_out);
  or or_9 (or_9_out, and_9_out, and_46_out, and_82_out);
  or or_10 (or_10_out, and_10_out, and_47_out, and_83_out);
  or or_11 (or_11_out, and_11_out, and_49_out, and_85_out);
  or or_12 (or_12_out, and_12_out, and_50_out, and_86_out);
  or or_13 (or_13_out, and_13_out, and_52_out, and_88_out);
  or or_14 (or_14_out, and_14_out, and_53_out, and_89_out);
  or or_15 (or_15_out, and_15_out, and_55_out, and_91_out);
  or or_16 (or_16_out, and_16_out, and_56_out, and_92_out);
  or or_17 (or_17_out, and_17_out, and_58_out, and_94_out);
  or or_18 (or_18_out, and_18_out, and_59_out, and_95_out);
  or or_19 (or_19_out, and_19_out, and_61_out, and_97_out);
  or or_20 (or_20_out, and_20_out, and_62_out, and_98_out);
  or or_21 (or_21_out, and_21_out, and_64_out, and_100_out);
  or or_22 (or_22_out, and_22_out, and_65_out, and_101_out);
  or or_23 (or_23_out, and_23_out, and_67_out, and_103_out);
  or or_24 (or_24_out, and_24_out, and_68_out, and_104_out);
  S_R_Flip_Flop s_r_ff_1 (.S(or_1_out), .clk(clock), .R(or_2_out), .Q(\output [0]));  // open: Qn, preset, reset, en
  S_R_Flip_Flop s_r_ff_2 (.S(or_3_out), .clk(clock), .R(or_4_out), .Q(\output [1]));  // open: Qn, preset, reset, en
  S_R_Flip_Flop s_r_ff_3 (.S(or_5_out), .clk(clock), .R(or_6_out), .Q(\output [2]));  // open: Qn, preset, reset, en
  S_R_Flip_Flop s_r_ff_4 (.S(or_7_out), .clk(clock), .R(or_8_out), .Q(\output [3]));  // open: Qn, preset, reset, en
  S_R_Flip_Flop s_r_ff_5 (.S(or_9_out), .clk(clock), .R(or_10_out), .Q(\output [4]));  // open: Qn, preset, reset, en
  S_R_Flip_Flop s_r_ff_6 (.S(or_11_out), .clk(clock), .R(or_12_out), .Q(\output [5]));  // open: Qn, preset, reset, en
  S_R_Flip_Flop s_r_ff_7 (.S(or_13_out), .clk(clock), .R(or_14_out), .Q(\output [6]));  // open: Qn, preset, reset, en
  S_R_Flip_Flop s_r_ff_8 (.S(or_15_out), .clk(clock), .R(or_16_out), .Q(\output [7]));  // open: Qn, preset, reset, en
  S_R_Flip_Flop s_r_ff_9 (.S(or_17_out), .clk(clock), .R(or_18_out), .Q(\output [8]));  // open: Qn, preset, reset, en
  S_R_Flip_Flop s_r_ff_10 (.S(or_19_out), .clk(clock), .R(or_20_out), .Q(\output [9]));  // open: Qn, preset, reset, en
  S_R_Flip_Flop s_r_ff_11 (.S(or_21_out), .clk(clock), .R(or_22_out), .Q(\output [10]));  // open: Qn, preset, reset, en
  S_R_Flip_Flop s_r_ff_12 (.S(or_23_out), .clk(clock), .R(or_24_out), .Q(\output [11]));  // open: Qn, preset, reset, en
  S_R_Flip_Flop s_r_ff_13 (
    .S(and_25_out), .clk(clock), .R(and_26_out), .Q(\output [12]));  // open: Qn, preset, reset, en
  S_R_Flip_Flop s_r_ff_14 (
    .S(and_27_out), .clk(clock), .R(and_28_out), .Q(\output [13]));  // open: Qn, preset, reset, en
  S_R_Flip_Flop s_r_ff_15 (
    .S(and_29_out), .clk(clock), .R(and_30_out), .Q(\output [14]));  // open: Qn, preset, reset, en
  S_R_Flip_Flop s_r_ff_16 (
    .S(and_31_out), .clk(clock), .R(and_32_out), .Q(\output [15]));  // open: Qn, preset, reset, en
endmodule

module main (
  input  [15:0] in_1,
  input  [15:0] in_2
);

  wire _900_901_out, A00_out, and_1_out, and_2_out, B00_out, B01_out, button_1_out, button_2_out,
       clock_1_out, counter_2_carry, cpu_1_intack, cpu_1_memwrt, D23_out, enter_reg_1_out, enter_reg_2_out,
       enter_reg_3_out, not_1_out, not_2_out, not_3_out, not_4_out, not_5_out, not_6_out, not_7_out,
       not_8_out, not_9_out, not_10_out, not_11_out, not_12_out, not_13_out, not_14_out, not_15_out,
       not_16_out, not_17_out, not_18_out, not_19_out, not_20_out, not_21_out, not_22_out, not_23_out,
       not_24_out, not_25_out, not_26_out, not_27_out, not_28_out, not_29_out, not_30_out, or_1_out,
       priority_encoder_1_en_out, priority_encoder_1_gs, s_r_ff_1_q, switch_1_rset_enter;
  wire [1:0] priority_encoder_2_out;
  wire [2:0] priority_encoder_1_out;
  wire [11:0] cpu_1_addr;
  wire [15:0] counter_1_q, cpu_1_datain, interruptswitch_1_data_out, interruptswitch_2_data_out,
       multiplexer_1_out, multiplexer_2_out, myregister_1_output, myregister_2_output, ram_1_data,
       switch_1_data_out;

  Counter #(.width(16), .max('hffff)) counter_1 (
    .Q(counter_1_q), .clk(clock_1_out));  // open: load, D, count, carry, clr
  Counter #(.width(10), .max('h3ff)) counter_2 (
    .carry(counter_2_carry), .clk(clock_1_out));  // open: load, D, count, Q, clr
  Clock clock_1 (.out(clock_1_out));
  and D23 (D23_out, cpu_1_addr[11], cpu_1_addr[10], ~cpu_1_addr[9], cpu_1_addr[8], ~cpu_1_addr[7], ~cpu_1_addr[6], cpu_1_addr[5], ~cpu_1_addr[4], ~cpu_1_addr[3], ~cpu_1_addr[2], cpu_1_addr[1], cpu_1_addr[0]);  // AND_Gate
  enter_reg enter_reg_1 (.inp(1'b1), .rst(switch_1_rset_enter), .clock(button_1_out), .out(enter_reg_1_out));
  Button button_1 (.out(button_1_out));
  Button button_2 (.out(button_2_out));
  enter_reg enter_reg_2 (.inp(1'b1), .rst(D23_out), .clock(counter_2_carry), .out(enter_reg_2_out));
  enter_reg enter_reg_3 (.inp(1'b1), .rst(A00_out), .clock(button_2_out), .out(enter_reg_3_out));
  and A00 (A00_out, cpu_1_addr[11], ~cpu_1_addr[10], cpu_1_addr[9], ~cpu_1_addr[8], ~cpu_1_addr[7], ~cpu_1_addr[6], ~cpu_1_addr[5], ~cpu_1_addr[4], ~cpu_1_addr[3], ~cpu_1_addr[2], ~cpu_1_addr[1], ~cpu_1_addr[0]);  // AND_Gate
  switch switch_1 (
    .data_in(in_1), .enter(enter_reg_1_out), .rset_enter(switch_1_rset_enter), .clock(clock_1_out),
    .rst(_900_901_out), .A0(cpu_1_addr[0]), .data_out(switch_1_data_out));
  interruptswitch interruptswitch_1 (
    .data_in(in_2), .enter(enter_reg_3_out), .clock(clock_1_out), .data_out(interruptswitch_1_data_out));
  interruptswitch interruptswitch_2 (
    .data_in(counter_1_q), .enter(enter_reg_2_out), .clock(clock_1_out), .data_out(interruptswitch_2_data_out));
  not not_1 (not_1_out, cpu_1_addr[4]);
  not not_2 (not_2_out, cpu_1_addr[10]);
  not not_3 (not_3_out, cpu_1_addr[9]);
  not not_4 (not_4_out, cpu_1_addr[6]);
  not not_5 (not_5_out, cpu_1_addr[7]);
  not not_6 (not_6_out, cpu_1_addr[5]);
  and _900_901 (_900_901_out, cpu_1_addr[11], not_2_out, not_3_out, cpu_1_addr[8], not_5_out, not_4_out, not_6_out, not_1_out, not_9_out, not_8_out, not_7_out);
  RAM #(.addrWidth(12), .dataWidth(16), .bus("separate")) ram_1 (
    .addr(cpu_1_addr), .din(cpu_1_datain), .data(ram_1_data), .str(cpu_1_memwrt), .clk(clock_1_out));  // open: sel, ld, clr
  cpu cpu_1 (
    .datOut(multiplexer_2_out), .\int (not_13_out), .addr(cpu_1_addr), .DataIn(cpu_1_datain),
    .memWrt(cpu_1_memwrt), .clock(clock_1_out), .intack(cpu_1_intack));
  not not_7 (not_7_out, cpu_1_addr[1]);
  not not_8 (not_8_out, cpu_1_addr[2]);
  not not_9 (not_9_out, cpu_1_addr[3]);
  not not_10 (not_10_out, cpu_1_addr[11]);
  not not_11 (not_11_out, cpu_1_addr[10]);
  not not_12 (not_12_out, cpu_1_addr[11]);
  and and_1 (and_1_out, not_10_out, not_11_out);
  or or_1 (or_1_out, and_1_out, and_2_out);
  Priority_Encoder priority_encoder_1 (
    .in3(enter_reg_3_out), .in6(enter_reg_2_out), .out(priority_encoder_1_out), .gs(priority_encoder_1_gs),
    .en_out(priority_encoder_1_en_out));  // open: in0, in1, in2, in4, in5, in7, en_in
  and and_2 (and_2_out, not_12_out, cpu_1_addr[10]);
  Priority_Encoder #(.select(2)) priority_encoder_2 (
    .in0(or_1_out), .in1(D23_out), .in2(A00_out), .in3(_900_901_out), .out(priority_encoder_2_out));  // open: gs, en_out, en_in
  not not_13 (not_13_out, priority_encoder_1_en_out);
  Multiplexer #(.select(2), .width(16)) multiplexer_1 (
    .in0(ram_1_data), .in1(interruptswitch_2_data_out), .in2(interruptswitch_1_data_out),
    .in3(switch_1_data_out), .out(multiplexer_1_out), .sel(priority_encoder_2_out));  // open: en
  Multiplexer #(.width(16)) multiplexer_2 (
    .in0(multiplexer_1_out), .in1({{13{1'b0}}, priority_encoder_1_out}), .out(multiplexer_2_out),
    .sel(cpu_1_intack));  // open: en
  not not_14 (not_14_out, cpu_1_addr[10]);
  not not_15 (not_15_out, cpu_1_addr[3]);
  not not_16 (not_16_out, cpu_1_addr[2]);
  not not_17 (not_17_out, cpu_1_addr[1]);
  not not_18 (not_18_out, cpu_1_addr[4]);
  not not_19 (not_19_out, cpu_1_addr[7]);
  not not_20 (not_20_out, cpu_1_addr[5]);
  not not_21 (not_21_out, cpu_1_addr[6]);
  and B00 (B00_out, cpu_1_addr[11], not_14_out, cpu_1_addr[9], cpu_1_addr[8], not_19_out, not_21_out, not_20_out, not_18_out, not_15_out, not_16_out, not_17_out, not_22_out);
  not not_22 (not_22_out, cpu_1_addr[0]);
  not not_23 (not_23_out, cpu_1_addr[7]);
  not not_24 (not_24_out, cpu_1_addr[10]);
  myRegister myregister_1 (
    .\input (cpu_1_datain), .ld(B00_out), .clock(clock_1_out), .\output (myregister_1_output));  // open: reset
  not not_25 (not_25_out, cpu_1_addr[2]);
  not not_26 (not_26_out, cpu_1_addr[4]);
  not not_27 (not_27_out, cpu_1_addr[1]);
  not not_28 (not_28_out, cpu_1_addr[3]);
  not not_29 (not_29_out, cpu_1_addr[5]);
  not not_30 (not_30_out, cpu_1_addr[6]);
  and B01 (B01_out, cpu_1_addr[11], not_24_out, cpu_1_addr[9], cpu_1_addr[8], not_23_out, not_30_out, not_29_out, not_26_out, not_28_out, not_25_out, not_27_out, cpu_1_addr[0]);
  Hex_Digit_Display hex_digit_display_1 (.value(myregister_1_output[15:12]));  // open: dp
  Hex_Digit_Display hex_digit_display_2 (.value(myregister_1_output[11:8]));  // open: dp
  myRegister myregister_2 (
    .\input (cpu_1_datain), .ld(B01_out), .clock(clock_1_out), .\output (myregister_2_output));  // open: reset
  Hex_Digit_Display hex_digit_display_3 (.value(myregister_1_output[3:0]));  // open: dp
  Hex_Digit_Display hex_digit_display_4 (.value(myregister_1_output[7:4]));  // open: dp
  S_R_Flip_Flop s_r_ff_1 (
    .S(A00_out), .clk(clock_1_out), .R(_900_901_out), .Q(s_r_ff_1_q));  // open: Qn, preset, reset, en
  Hex_Digit_Display hex_digit_display_5 (.value(myregister_2_output[11:8]));  // open: dp
  Hex_Digit_Display hex_digit_display_6 (.value(myregister_2_output[15:12]));  // open: dp
  LED led_1 (.in(s_r_ff_1_q));
  Hex_Digit_Display hex_digit_display_7 (.value(myregister_2_output[3:0]));  // open: dp
  Hex_Digit_Display hex_digit_display_8 (.value(myregister_2_output[7:4]));  // open: dp
endmodule

module switch (
  input  [15:0] data_in,
  input  enter,
  input  clock,
  input  rst,
  input  A0,
  output [15:0] data_out,
  output rset_enter
);

  wire not_1_out;
  wire [15:0] myregister_1_output, myregister_2_output;

  myRegister myregister_1 (
    .\input (data_in), .ld(enter), .clock(clock), .\output (myregister_1_output));  // open: reset
  myRegister myregister_2 (
    .\input (16'h1), .reset(rset_enter), .ld(enter), .clock(clock), .\output (myregister_2_output));
  not not_1 (not_1_out, A0);
  and and_1 (rset_enter, not_1_out, rst);
  Multiplexer #(.width(16)) multiplexer_1 (
    .in0(myregister_1_output), .in1(myregister_2_output), .out(data_out), .sel(A0));  // open: en
endmodule

module enter_reg (
  input  rst,
  input  inp,
  input  clock,
  output out
);

  wire and_1_out, and_2_out, not_1_out;

  not not_1 (not_1_out, inp);
  and and_1 (and_1_out, inp, 1'b1);
  and and_2 (and_2_out, not_1_out, 1'b1);
  S_R_Flip_Flop s_r_ff_1 (.S(and_1_out), .clk(clock), .R(and_2_out), .Q(out), .reset(rst));  // open: Qn, preset, en
endmodule

module interruptswitch (
  input  [15:0] data_in,
  input  enter,
  input  clock,
  output [15:0] data_out
);

  myRegister myregister_1 (.\input (data_in), .ld(enter), .clock(clock), .\output (data_out));  // open: reset
endmodule

module regSti (
  input  Zf_ALU,
  input  ZfLoad_Ctrl,
  input  STI,
  input  reset,
  input  CLI,
  input  [15:0] \input ,
  input  ld,
  input  clock,
  output [15:0] \output 
);

  wire and_1_out, and_2_out, and_3_out, and_4_out, and_5_out, and_6_out, and_7_out, and_8_out, and_9_out,
       and_10_out, and_11_out, and_12_out, and_13_out, and_14_out, and_15_out, and_16_out, and_17_out,
       and_18_out, and_19_out, and_20_out, and_21_out, and_22_out, and_23_out, and_24_out, and_25_out,
       and_26_out, and_27_out, and_28_out, and_29_out, and_30_out, and_31_out, and_32_out, and_33_out,
       and_34_out, and_35_out, and_36_out, not_1_out, not_2_out, not_3_out, not_4_out, not_5_out, not_6_out,
       not_7_out, not_8_out, not_9_out, not_10_out, not_11_out, not_12_out, not_13_out, not_14_out,
       not_15_out, not_16_out, or_1_out, or_2_out, or_3_out, or_4_out;

  not not_1 (not_1_out, \input [0]);
  not not_2 (not_2_out, \input [1]);
  not not_3 (not_3_out, \input [2]);
  not not_4 (not_4_out, \input [3]);
  not not_5 (not_5_out, \input [4]);
  not not_6 (not_6_out, \input [5]);
  not not_7 (not_7_out, \input [6]);
  not not_8 (not_8_out, \input [7]);
  not not_9 (not_9_out, \input [8]);
  not not_10 (not_10_out, \input [9]);
  not not_11 (not_11_out, \input [10]);
  not not_12 (not_12_out, \input [11]);
  not not_13 (not_13_out, \input [12]);
  not not_14 (not_14_out, \input [13]);
  not not_15 (not_15_out, \input [14]);
  not not_16 (not_16_out, \input [15]);
  and and_1 (and_1_out, \input [0], ld);
  and and_2 (and_2_out, not_1_out, ld);
  and and_3 (and_3_out, \input [1], ld);
  and and_4 (and_4_out, not_2_out, ld);
  and and_5 (and_5_out, \input [2], ld);
  and and_6 (and_6_out, not_3_out, ld);
  and and_7 (and_7_out, \input [3], ld);
  and and_8 (and_8_out, not_4_out, ld);
  and and_9 (and_9_out, \input [4], ld);
  and and_10 (and_10_out, not_5_out, ld);
  and and_11 (and_11_out, \input [5], ld);
  and and_12 (and_12_out, not_6_out, ld);
  and and_13 (and_13_out, \input [6], ld);
  and and_14 (and_14_out, not_7_out, ld);
  and and_15 (and_15_out, \input [7], ld);
  and and_16 (and_16_out, not_8_out, ld);
  and and_17 (and_17_out, \input [8], ld);
  and and_18 (and_18_out, not_9_out, ld);
  and and_19 (and_19_out, \input [9], ld);
  and and_20 (and_20_out, not_10_out, ld);
  and and_21 (and_21_out, \input [10], ld);
  and and_22 (and_22_out, not_11_out, ld);
  and and_23 (and_23_out, \input [11], ld);
  and and_24 (and_24_out, not_12_out, ld);
  and and_25 (and_25_out, \input [12], ld);
  and and_26 (and_26_out, not_13_out, ld);
  and and_27 (and_27_out, \input [13], ld);
  and and_28 (and_28_out, not_14_out, ld);
  and and_29 (and_29_out, \input [14], ld);
  and and_30 (and_30_out, not_15_out, ld);
  and and_31 (and_31_out, \input [15], ld);
  and and_32 (and_32_out, not_16_out, ld);
  and and_33 (and_33_out, STI, 1'b1);
  and and_34 (and_34_out, CLI, 1'b1);
  and and_35 (and_35_out, Zf_ALU, ZfLoad_Ctrl);
  or or_1 (or_1_out, and_35_out, and_1_out);
  and and_36 (and_36_out, ~Zf_ALU, ZfLoad_Ctrl);  // AND_Gate
  or or_2 (or_2_out, and_36_out, and_2_out);
  or or_3 (or_3_out, and_33_out, and_3_out);
  or or_4 (or_4_out, and_34_out, and_4_out);
  S_R_Flip_Flop s_r_ff_1 (
    .S(or_1_out), .clk(clock), .R(or_2_out), .Q(\output [0]), .reset(reset));  // open: Qn, preset, en
  S_R_Flip_Flop s_r_ff_2 (
    .S(or_3_out), .clk(clock), .R(or_4_out), .Q(\output [1]), .reset(reset));  // open: Qn, preset, en
  S_R_Flip_Flop s_r_ff_3 (
    .S(and_5_out), .clk(clock), .R(and_6_out), .Q(\output [2]), .reset(reset));  // open: Qn, preset, en
  S_R_Flip_Flop s_r_ff_4 (
    .S(and_7_out), .clk(clock), .R(and_8_out), .Q(\output [3]), .reset(reset));  // open: Qn, preset, en
  S_R_Flip_Flop s_r_ff_5 (
    .S(and_9_out), .clk(clock), .R(and_10_out), .Q(\output [4]), .reset(reset));  // open: Qn, preset, en
  S_R_Flip_Flop s_r_ff_6 (
    .S(and_11_out), .clk(clock), .R(and_12_out), .Q(\output [5]), .reset(reset));  // open: Qn, preset, en
  S_R_Flip_Flop s_r_ff_7 (
    .S(and_13_out), .clk(clock), .R(and_14_out), .Q(\output [6]), .reset(reset));  // open: Qn, preset, en
  S_R_Flip_Flop s_r_ff_8 (
    .S(and_15_out), .clk(clock), .R(and_16_out), .Q(\output [7]), .reset(reset));  // open: Qn, preset, en
  S_R_Flip_Flop s_r_ff_9 (
    .S(and_17_out), .clk(clock), .R(and_18_out), .Q(\output [8]), .reset(reset));  // open: Qn, preset, en
  S_R_Flip_Flop s_r_ff_10 (
    .S(and_19_out), .clk(clock), .R(and_20_out), .Q(\output [9]), .reset(reset));  // open: Qn, preset, en
  S_R_Flip_Flop s_r_ff_11 (
    .S(and_21_out), .clk(clock), .R(and_22_out), .Q(\output [10]), .reset(reset));  // open: Qn, preset, en
  S_R_Flip_Flop s_r_ff_12 (
    .S(and_23_out), .clk(clock), .R(and_24_out), .Q(\output [11]), .reset(reset));  // open: Qn, preset, en
  S_R_Flip_Flop s_r_ff_13 (
    .S(and_25_out), .clk(clock), .R(and_26_out), .Q(\output [12]), .reset(reset));  // open: Qn, preset, en
  S_R_Flip_Flop s_r_ff_14 (
    .S(and_27_out), .clk(clock), .R(and_28_out), .Q(\output [13]), .reset(reset));  // open: Qn, preset, en
  S_R_Flip_Flop s_r_ff_15 (
    .S(and_29_out), .clk(clock), .R(and_30_out), .Q(\output [14]), .reset(reset));  // open: Qn, preset, en
  S_R_Flip_Flop s_r_ff_16 (
    .S(and_31_out), .clk(clock), .R(and_32_out), .Q(\output [15]), .reset(reset));  // open: Qn, preset, en
endmodule

module _6bitreg (
  input  [5:0] \input ,
  input  clock,
  output [5:0] \output 
);

  wire and_1_out, and_2_out, and_3_out, and_4_out, and_5_out, and_6_out, and_7_out, and_8_out, and_9_out,
       and_10_out, and_11_out, and_12_out, not_1_out, not_2_out, not_3_out, not_4_out, not_5_out, not_6_out;

  not not_1 (not_1_out, \input [0]);
  not not_2 (not_2_out, \input [1]);
  not not_3 (not_3_out, \input [2]);
  not not_4 (not_4_out, \input [3]);
  not not_5 (not_5_out, \input [4]);
  not not_6 (not_6_out, \input [5]);
  and and_1 (and_1_out, \input [0], 1'b1);
  and and_2 (and_2_out, not_1_out, 1'b1);
  and and_3 (and_3_out, \input [1], 1'b1);
  and and_4 (and_4_out, not_2_out, 1'b1);
  and and_5 (and_5_out, \input [2], 1'b1);
  and and_6 (and_6_out, not_3_out, 1'b1);
  and and_7 (and_7_out, \input [3], 1'b1);
  and and_8 (and_8_out, not_4_out, 1'b1);
  and and_9 (and_9_out, \input [4], 1'b1);
  and and_10 (and_10_out, not_5_out, 1'b1);
  and and_11 (and_11_out, \input [5], 1'b1);
  and and_12 (and_12_out, not_6_out, 1'b1);
  S_R_Flip_Flop s_r_ff_1 (.S(and_1_out), .clk(clock), .R(and_2_out), .Q(\output [0]));  // open: Qn, preset, reset, en
  S_R_Flip_Flop s_r_ff_2 (.S(and_3_out), .clk(clock), .R(and_4_out), .Q(\output [1]));  // open: Qn, preset, reset, en
  S_R_Flip_Flop s_r_ff_3 (.S(and_5_out), .clk(clock), .R(and_6_out), .Q(\output [2]));  // open: Qn, preset, reset, en
  S_R_Flip_Flop s_r_ff_4 (.S(and_7_out), .clk(clock), .R(and_8_out), .Q(\output [3]));  // open: Qn, preset, reset, en
  S_R_Flip_Flop s_r_ff_5 (.S(and_9_out), .clk(clock), .R(and_10_out), .Q(\output [4]));  // open: Qn, preset, reset, en
  S_R_Flip_Flop s_r_ff_6 (.S(and_11_out), .clk(clock), .R(and_12_out), .Q(\output [5]));  // open: Qn, preset, reset, en
endmodule

module _12bitreg (
  input  reset,
  input  [11:0] \input ,
  input  load,
  input  clock,
  output [11:0] \output 
);

  wire and_1_out, and_2_out, and_3_out, and_4_out, and_5_out, and_6_out, and_7_out, and_8_out, and_9_out,
       and_10_out, and_11_out, and_12_out, and_13_out, and_14_out, and_15_out, and_16_out, and_17_out,
       and_18_out, and_19_out, and_20_out, and_21_out, and_22_out, and_23_out, and_24_out, not_1_out,
       not_2_out, not_3_out, not_4_out, not_5_out, not_6_out, not_7_out, not_8_out, not_9_out, not_10_out,
       not_11_out, not_12_out;

  not not_1 (not_1_out, \input [0]);
  not not_2 (not_2_out, \input [1]);
  not not_3 (not_3_out, \input [2]);
  not not_4 (not_4_out, \input [3]);
  not not_5 (not_5_out, \input [4]);
  not not_6 (not_6_out, \input [5]);
  not not_7 (not_7_out, \input [6]);
  not not_8 (not_8_out, \input [7]);
  not not_9 (not_9_out, \input [8]);
  not not_10 (not_10_out, \input [9]);
  not not_11 (not_11_out, \input [10]);
  not not_12 (not_12_out, \input [11]);
  and and_1 (and_1_out, \input [0], load);
  and and_2 (and_2_out, not_1_out, load);
  and and_3 (and_3_out, \input [1], load);
  and and_4 (and_4_out, not_2_out, load);
  and and_5 (and_5_out, \input [2], load);
  and and_6 (and_6_out, not_3_out, load);
  and and_7 (and_7_out, \input [3], load);
  and and_8 (and_8_out, not_4_out, load);
  and and_9 (and_9_out, \input [4], load);
  and and_10 (and_10_out, not_5_out, load);
  and and_11 (and_11_out, \input [5], load);
  and and_12 (and_12_out, not_6_out, load);
  and and_13 (and_13_out, \input [6], load);
  and and_14 (and_14_out, not_7_out, load);
  and and_15 (and_15_out, \input [7], load);
  and and_16 (and_16_out, not_8_out, load);
  and and_17 (and_17_out, \input [8], load);
  and and_18 (and_18_out, not_9_out, load);
  and and_19 (and_19_out, \input [9], load);
  and and_20 (and_20_out, not_10_out, load);
  and and_21 (and_21_out, \input [10], load);
  and and_22 (and_22_out, not_11_out, load);
  and and_23 (and_23_out, \input [11], load);
  and and_24 (and_24_out, not_12_out, load);
  S_R_Flip_Flop s_r_ff_1 (
    .S(and_1_out), .clk(clock), .R(and_2_out), .Q(\output [0]), .reset(reset));  // open: Qn, preset, en
  S_R_Flip_Flop s_r_ff_2 (
    .S(and_3_out), .clk(clock), .R(and_4_out), .Q(\output [1]), .reset(reset));  // open: Qn, preset, en
  S_R_Flip_Flop s_r_ff_3 (
    .S(and_5_out), .clk(clock), .R(and_6_out), .Q(\output [2]), .reset(reset));  // open: Qn, preset, en
  S_R_Flip_Flop s_r_ff_4 (
    .S(and_7_out), .clk(clock), .R(and_8_out), .Q(\output [3]), .reset(reset));  // open: Qn, preset, en
  S_R_Flip_Flop s_r_ff_5 (
    .S(and_9_out), .clk(clock), .R(and_10_out), .Q(\output [4]), .reset(reset));  // open: Qn, preset, en
  S_R_Flip_Flop s_r_ff_6 (
    .S(and_11_out), .clk(clock), .R(and_12_out), .Q(\output [5]), .reset(reset));  // open: Qn, preset, en
  S_R_Flip_Flop s_r_ff_7 (
    .S(and_13_out), .clk(clock), .R(and_14_out), .Q(\output [6]), .reset(reset));  // open: Qn, preset, en
  S_R_Flip_Flop s_r_ff_8 (
    .S(and_15_out), .clk(clock), .R(and_16_out), .Q(\output [7]), .reset(reset));  // open: Qn, preset, en
  S_R_Flip_Flop s_r_ff_9 (
    .S(and_17_out), .clk(clock), .R(and_18_out), .Q(\output [8]), .reset(reset));  // open: Qn, preset, en
  S_R_Flip_Flop s_r_ff_10 (
    .S(and_19_out), .clk(clock), .R(and_20_out), .Q(\output [9]), .reset(reset));  // open: Qn, preset, en
  S_R_Flip_Flop s_r_ff_11 (
    .S(and_21_out), .clk(clock), .R(and_22_out), .Q(\output [10]), .reset(reset));  // open: Qn, preset, en
  S_R_Flip_Flop s_r_ff_12 (
    .S(and_23_out), .clk(clock), .R(and_24_out), .Q(\output [11]), .reset(reset));  // open: Qn, preset, en
endmodule

module _6bitreg2 (
  input  clk,
  input  [5:0] \input ,
  output [5:0] \output 
);

  wire not_1_out, not_2_out, not_3_out, not_4_out, not_5_out, not_6_out;

  not not_1 (not_1_out, \input [0]);
  not not_2 (not_2_out, \input [1]);
  not not_3 (not_3_out, \input [2]);
  not not_4 (not_4_out, \input [3]);
  not not_5 (not_5_out, \input [4]);
  not not_6 (not_6_out, \input [5]);
  S_R_Flip_Flop s_r_ff_1 (
    .S(\input [0]), .clk(clk), .R(not_1_out), .Q(\output [0]), .preset(1'b0), .reset(1'b0), .en(1'b1));  // open: Qn
  S_R_Flip_Flop s_r_ff_2 (
    .S(\input [1]), .clk(clk), .R(not_2_out), .Q(\output [1]), .preset(1'b0), .reset(1'b0), .en(1'b1));  // open: Qn
  S_R_Flip_Flop s_r_ff_3 (
    .S(\input [2]), .clk(clk), .R(not_3_out), .Q(\output [2]), .preset(1'b0), .reset(1'b0), .en(1'b1));  // open: Qn
  S_R_Flip_Flop s_r_ff_4 (
    .S(\input [3]), .clk(clk), .R(not_4_out), .Q(\output [3]), .preset(1'b0), .reset(1'b0), .en(1'b1));  // open: Qn
  S_R_Flip_Flop s_r_ff_5 (
    .S(\input [4]), .clk(clk), .R(not_5_out), .Q(\output [4]), .preset(1'b0), .reset(1'b0), .en(1'b1));  // open: Qn
  S_R_Flip_Flop s_r_ff_6 (
    .S(\input [5]), .clk(clk), .R(not_6_out), .Q(\output [5]), .preset(1'b0), .reset(1'b0), .en(1'b1));  // open: Qn
endmodule
